# Fritzing sketch sketch (saved by Fritzing 0.9.4)
breadboards: 1

parts:
  Компонент1 = Arduino Uno (Rev3)
  Компонент2 = IR Receiver Breakout [package=PCB]
  LED3 = smd LED [color="Red (633nm)" package="0603 [SMD]"]
  LED5 = RGB LED (com. anode, rbg) [package="5 mm [THT]"]
  R1 = Resistor [tolerance=±5% resistance=220 package="0603 [SMD]"]
  R2 = Resistor [tolerance=±5% resistance=220 package="0603 [SMD]"]
  R3 = Resistor [tolerance=±5% resistance=220 package="0603 [SMD]"]
  R4 = Resistor [tolerance=±5% resistance=220 package="0603 [SMD]"]

nets:
  N1: Компонент1.D11_PWM/MOSI, R1.Pin_1
  GND: Компонент1.GND, Компонент2.GND, LED3.cathode, LED5.common_anode
  N2: Компонент1.D2, Компонент2.VCC
  N3: Компонент1.D3_PWM, R4.Pin_1
  N4: Компонент1.D5_PWM, R3.Pin_1
  N5: Компонент1.D6_PWM, R2.Pin_1
  N6: Компонент1.3V3, Компонент2.OUT
  N7: LED3.anode, R1.Pin_0
  N8: LED5.red_cathode, R4.Pin_0
  N9: LED5.blue_cathode, R2.Pin_0
  N10: LED5.green_cathode, R3.Pin_0
